# Fritzing sketch Werto (saved by Fritzing 0.9.3b)
breadboards: 1

parts:
  RHT1 = Humidity and Temperature Sensor RHT03 [part_number=DHT22]
  WeMos_D1_Mini1 = WeMos D1 Mini
  Mod1 = KY-019 5V Relay Module [package="Breakout board"]
  WATER_PUMP1 = water pump/motor  # not connected
  Chirp!_Soil_Moisture_Sensor1 = Chirp! Soil Moisture Sensor v2.7.3
  Mod2 = KY-019 5V Relay Module [package="Breakout board"]
  YwRobot_Power_Supply1 = YwRobot Breadboard Power Supply [part_number=545043]
  VCC1 = Battery block 9V  # not connected
  WATER_PUMP2 = water pump/motor  # not connected
  F1 = Fan - Ventilador [package=THT]

nets:
  VCC: RHT1.Vcc, WeMos_D1_Mini1.3V3, Chirp!_Soil_Moisture_Sensor1.Pin_1, YwRobot_Power_Supply1.VCC#5, YwRobot_Power_Supply1.VCC#6
  N1: RHT1.GND_2, Chirp!_Soil_Moisture_Sensor1.pin_5, YwRobot_Power_Supply1.GND#11, YwRobot_Power_Supply1.GND#12
  N2: WeMos_D1_Mini1.G, Mod1.-, Mod1.NO, Mod2.-, Mod2.NO, YwRobot_Power_Supply1.GND#13, YwRobot_Power_Supply1.GND#14, F1.GND
  N3: Mod1.+, Mod2.+, YwRobot_Power_Supply1.VCC#9, YwRobot_Power_Supply1.VCC#10, F1.5V

notes:
  DHT22

custom parts:
  KY-019 5V Relay Module: KY-019 5V Relay module, used to control AC circuits. (Special thanks to vanepp for fixing the PCB holes and other errors)
  water pump/motor: WATER PUMP BY ARDUBLOCKTR
  YwRobot Breadboard Power Supply: The YwRobot Breadboard Power Supply (MB-V2) has two power rails; they can be 5V or 3V3. Power to the module can be provided through the female USB socket or through the A10 (female) 2.1mm power jack.
  Fan - Ventilador: Ventilador de 2 pines, se encuentra comunmente en computadoras de escritorio

// code stored in the sketch: AnalogReadSerial2LCD_LED.ino
#include <Wire.h>
#include <LiquidCrystal_I2C.h>

LiquidCrystal_I2C lcd(0x27, 16, 2);   // adress and format LCD

const int analogInPin = A0;           // Analog input pin that the potentiometer is attached to
const int analogOutPin = 9;           // Analog output pin that the LED is attached to

int sensorValue = 0;                  // value read from the pot
int outputValue = 0;                  // value output to the PWM (analog out)

void setup() {
  lcd.init();                         // init LCD
  lcd.backlight();
  lcd.home();
  lcd.setCursor(5, 0);                // place static text
  lcd.print("ADC = ");
  lcd.setCursor(15, 0);
  lcd.print("V");
  lcd.setCursor(0, 1);
  lcd.print("LED : ");
  lcd.setCursor(12, 1);
  lcd.print("%");
  Serial.begin(9600);                 // optional serial monitor
}

void loop() {
  int sensorValue = analogRead(analogInPin);          // read analog A0 en store in sensorValue
  float voltValue = 5.0 / 1024.0 * sensorValue;       // calculate volt at analog A0 and store in voltValue
  float percentValue = sensorValue / 1024.0 * 100.0;  // calculate percentage analog A0 and store in percentValue
  outputValue = map(sensorValue, 0, 1023, 0, 255);    // map analog input to analog output and store in outputValue
  analogWrite(analogOutPin, outputValue);             // write outputValue to analogOutPin

  lcd.setCursor(0, 0);                                // set cursor at deserid position
  leadingZeros(sensorValue, 4);                       // print sensorvalue with number of leading-characters (0 or space as specified in function leadingZeros)
  lcd.setCursor(10, 0);                               // set cursor at deserid position
  lcd.print(voltValue);                               // print voltValue
  lcd.setCursor(6, 1);                                // set cursor at deserid position
  lcd.print(percentValue);                            // print percentValue

  Serial.print("sensor = " );                         // print the results to the serial monitor:
  Serial.print(sensorValue);
  Serial.print("\t output = ");
  Serial.print(outputValue);
  Serial.print("\t procent = ");
  Serial.println(percentValue);

  delay(1000);                                        // set delay
}

void leadingZeros( int value, int width) {            // display result with leading characters
  char valueStr[6];                                   // large enough to hold an int
  itoa (value, valueStr, 10);                         // itoa converts int to string
  int len = strlen(valueStr);                         // calculate length of valueStr
  if (len < width) {
    len = width - len;
    while (len--)
      lcd.print(' ');                                 // for leading zeros place '0' between (), for leading spaces place ' ' between ()
  }
  lcd.print(valueStr);
}

// code stored in the sketch: Huerto.ino
// Me cago


#include "config.h"
#include "DHT.h"


#define DHTPIN 5
#define DHTTYPE DHT22   // DHT 22  (AM2302), AM2321
#define SENHUM A0
#define RELE_AGUA 14
#define RELE_FERT 12


// set up the 'digital' feed Estos comentarios no valen


AdafruitIO_Feed *temperaturaFeed = io.feed("temperatura");
AdafruitIO_Feed *humedadFeed = io.feed("humedad");
AdafruitIO_Feed *humedadSueloFeed = io.feed("humedadtierra");
AdafruitIO_Feed *bombaaguaFeed = io.feed("bombaagua");
AdafruitIO_Feed *bombafertFeed = io.feed("bombafert");


// Initialize DHT sensor.
// Note that older versions of this library took an optional third parameter to
// tweak the timings for faster processors.  This parameter is no longer needed
// as the current DHT reading algorithm adjusts itself to work on faster procs. Carlos no los leas


DHT dht(DHTPIN, DHTTYPE);


void setup() {


  // start the serial connection No
  Serial.begin(115200);
  Serial.println("ESP8266 ha arrancado correctamente.");
  dht.begin();
  Serial.println("DHT bien.");
  //analogSetPinAttenuation(SENHUM, ADC_11db);


  
  pinMode(RELE_AGUA, OUTPUT);
  pinMode(RELE_FERT, OUTPUT);
  Serial.println("Pin modes bien.");
  // wait for serial monitor to open
  while(! Serial);
  
  // connect to io.adafruit.com
  Serial.print("Connecting to Adafruit IO");
  io.connect();
  
// set up a message handler for the 'relay' feed.Para de leerlos
  // the handleMessage function (defined below)
  // will be called whenever a message is
  // received from adafruit io
  bombaaguaFeed->onMessage(handleMessage);
  bombafertFeed->onMessage(handleMessage1);
  Serial.println("Handlers bien");
  // wait for a connection
  while(io.status() < AIO_CONNECTED) {
    Serial.print(".");
    yield();
    delay(500);
  }


  // we are connected
  Serial.println();
  Serial.println(io.statusText());
  
  // Get the last known value from the feed
  bombaaguaFeed->get();
  bombafertFeed->get();
  Serial.println("Bombas guardadas.");
}


void loop() {


  // io.run(); is required for all sketches. Al final te escupo.
  // it should always be present at the top of your loop
  // function. it keeps the client connected to
  // io.adafruit.com, and processes any incoming data.
  io.run();
  
  float h = dht.readHumidity();
  float t = dht.readTemperature();
  float f = analogRead(SENHUM);
  
  // Conversión lectura analogica en porcentaje. 
  f = map(f, 1023, 330, 0, 100);
  
  // save the current state to the 'digital' feed on adafruit io
  Serial.print(F("Humedad ambiental: "));
  Serial.println(h);
  Serial.print(F("Temperatura: "));
  Serial.println(t);
  Serial.print(F("Humedad suelo: "));
  Serial.println(f);
  Serial.println("--------------------------");
  


  humedadFeed->save(h);
  temperaturaFeed->save(t);
  humedadSueloFeed->save(f);
  yield();
  delay(10000);


}


void handleMessage(AdafruitIO_Data *data) {


  Serial.print("Mensaje recibido en bomba de agua. ");
  Serial.println(data->toChar());


// Check to see if the morning scheduled trigger has executed Me cago
  if (strcmp(data->toChar(), "1") == 0) {
      Serial.println("Encendiendo bomba de agua. ");
      digitalWrite(RELE_AGUA, LOW);
  }
// Check to see if the evening scheduled action has executed
  else if (strcmp(data->toChar(), "0") == 0) {
      Serial.println("Apagando bomba de agua. ");
      digitalWrite(RELE_AGUA, HIGH);
  }
  else {
      Serial.println("Datos inesperados en bomba de agua. ");
  }
}


void handleMessage1(AdafruitIO_Data *data) {


  Serial.print("Mensaje recibido en bomba de fertilizante. ");
  Serial.println(data->toChar());


// Check to see if the morning scheduled trigger has executed
  if (strcmp(data->toChar(), "1") == 0) {
      Serial.println("Activando bomba fertilizante. ");
      digitalWrite(RELE_FERT, LOW);
  }
// Check to see if the evening scheduled action has executed 
  else if (strcmp(data->toChar(), "0") == 0) {
      Serial.println("Desactivando bomba fertilizante. ");
      digitalWrite(RELE_FERT, HIGH);
  }
  else {
      Serial.println("Datos inesperados en bomba fertilizante. ");
  }
}
